# Fritzing sketch 1_digito_7_segmentos (saved by Fritzing 0.9.2b)
breadboards: 1

parts:
  7_Segment1 = 7 Segment Display
  R1 = Resistor [tolerance=±5% resistance=270 package=THT]
  R2 = Resistor [tolerance=±5% resistance=270 package=THT]
  R3 = Resistor [tolerance=±5% resistance=270 package=THT]
  R4 = Resistor [tolerance=±5% resistance=270 package=THT]
  R5 = Resistor [tolerance=±5% resistance=270 package=THT]
  R6 = Resistor [tolerance=±5% resistance=270 package=THT]
  R7 = Resistor [tolerance=±5% resistance=270 package=THT]
  R8 = Resistor [tolerance=±5% resistance=270 package=THT]
  Parte1 = Arduino Uno (Rev3)
  S1 = Pushbutton [package="[THT]"]
  R17 = Resistor [tolerance=±5% resistance=10k package=THT]

nets:
  N1: 7_Segment1.Segment_E, R3.Pin_1
  N2: 7_Segment1.Segment_D, R4.Pin_1
  GND: 7_Segment1.common_cathode, Parte1.GND, R17.Pin_1
  N3: 7_Segment1.Segment_C, R5.Pin_1
  N4: 7_Segment1.Segment_DP, R8.Pin_1
  N5: 7_Segment1.Segment_B, R6.Pin_1
  N6: 7_Segment1.Segment_A, R7.Pin_1
  N7: 7_Segment1.Segment_F, R2.Pin_1
  N8: 7_Segment1.Segment_G, R1.Pin_1
  N9: R1.Pin_0, Parte1.D3_PWM
  N10: R2.Pin_0, Parte1.D4
  N11: R3.Pin_0, Parte1.D5_PWM
  N12: R4.Pin_0, Parte1.D6_PWM
  N13: R5.Pin_0, Parte1.D7
  N14: R6.Pin_0, Parte1.D8
  N15: R7.Pin_0, Parte1.D9_PWM
  N16: R8.Pin_0, Parte1.D2
  N17: Parte1.D11_PWM/MOSI, S1.Pin_3, S1.Pin_4, R17.Pin_0
  5V: Parte1.5V, S1.Pin_1, S1.Pin_2
