# Fritzing sketch 2_digitos_7_segmentos_y_2_registros_desplazamiento (saved by Fritzing 0.9.2b)
breadboards: 1

parts:
  7_Segment1 = 7 Segment Display
  7_Segment2 = 7 Segment Display
  R1 = Resistor [tolerance=±5% resistance=270 package=THT]
  R2 = Resistor [tolerance=±5% resistance=270 package=THT]
  R3 = Resistor [tolerance=±5% resistance=270 package=THT]
  R4 = Resistor [tolerance=±5% resistance=270 package=THT]
  R5 = Resistor [tolerance=±5% resistance=270 package=THT]
  R6 = Resistor [tolerance=±5% resistance=270 package=THT]
  R7 = Resistor [tolerance=±5% resistance=270 package=THT]
  R8 = Resistor [tolerance=±5% resistance=270 package=THT]
  U1 = 74HC595 [package="DIP16 [THT]"]
  R9 = Resistor [tolerance=±5% resistance=270 package=THT]
  R10 = Resistor [tolerance=±5% resistance=270 package=THT]
  R11 = Resistor [tolerance=±5% resistance=270 package=THT]
  R12 = Resistor [tolerance=±5% resistance=270 package=THT]
  R13 = Resistor [tolerance=±5% resistance=270 package=THT]
  R14 = Resistor [tolerance=±5% resistance=270 package=THT]
  R15 = Resistor [tolerance=±5% resistance=270 package=THT]
  R16 = Resistor [tolerance=±5% resistance=270 package=THT]
  U2 = 74HC595 [package="DIP16 [THT]"]
  Parte1 = Arduino Uno (Rev3)
  S1 = Pushbutton [package="[THT]"]
  R17 = Resistor [tolerance=±5% resistance=10k package=THT]

nets:
  N1: 7_Segment1.Segment_E, R3.Pin_1
  N2: 7_Segment1.Segment_D, R4.Pin_1
  GND: 7_Segment1.common_cathode, 7_Segment2.common_cathode, U1.GND, U1.OE, U2.GND, U2.OE, Parte1.GND, R17.Pin_1
  N3: 7_Segment1.Segment_C, R5.Pin_1
  N4: 7_Segment1.Segment_DP, R8.Pin_1
  N5: 7_Segment1.Segment_B, R6.Pin_1
  N6: 7_Segment1.Segment_A, R7.Pin_1
  N7: 7_Segment1.Segment_F, R2.Pin_1
  N8: 7_Segment1.Segment_G, R1.Pin_1
  N9: 7_Segment2.Segment_E, R12.Pin_1
  N10: 7_Segment2.Segment_D, R14.Pin_1
  N11: 7_Segment2.Segment_C, R9.Pin_1
  N12: 7_Segment2.Segment_DP, R10.Pin_1
  N13: 7_Segment2.Segment_B, R13.Pin_1
  N14: 7_Segment2.Segment_A, R16.Pin_1
  N15: 7_Segment2.Segment_F, R11.Pin_1
  N16: 7_Segment2.Segment_G, R15.Pin_1
  N17: R1.Pin_0, U1.Q6
  N18: R2.Pin_0, U1.Q5
  N19: R3.Pin_0, U1.Q4
  N20: R4.Pin_0, U1.Q3
  N21: R5.Pin_0, U1.Q2
  N22: R6.Pin_0, U1.Q1
  N23: R7.Pin_0, U1.Q0
  N24: R8.Pin_0, U1.Q7
  N25: U1.Q7', U2.DS
  5V: U1.MR, U1.VCC, U2.MR, U2.VCC, Parte1.5V, S1.Pin_1, S1.Pin_2
  N26: U1.SH_CP, U2.SH_CP, Parte1.D10_PWM/SS
  N27: U1.ST_CP, U2.ST_CP, Parte1.D9_PWM
  N28: U1.DS, Parte1.D8
  N29: R9.Pin_0, U2.Q2
  N30: R10.Pin_0, U2.Q7
  N31: R11.Pin_0, U2.Q5
  N32: R12.Pin_0, U2.Q4
  N33: R13.Pin_0, U2.Q1
  N34: R14.Pin_0, U2.Q3
  N35: R15.Pin_0, U2.Q6
  N36: R16.Pin_0, U2.Q0
  N37: Parte1.D6_PWM, S1.Pin_3, S1.Pin_4, R17.Pin_0
